# Fritzing sketch VacStatus (saved by Fritzing 1.0.1rc)
breadboards: 1

parts:
  A1 = Particle - Photon2
  J2 = Power Jack [package=power_jack_slot]
  LED1 = smd LED [color="Red (633nm)" package="0805 [SMD]"]
  R1 = Resistor [tolerance=±5% resistance=220 package="0805 [SMD]"]
  S1 = Pushbutton [package="[THT]"]

nets:
  3.3V: A1.Pin_2, S1.Pin_3, S1.Pin_4
  GND: A1.Pin_4, J2.GND, LED1.anode
  N1: A1.Pin_7, S1.Pin_1, S1.Pin_2
  N2: A1.Pin_18, R1.Pin_0
  N3: A1.Pin_26, J2.PWR
  N4: LED1.cathode, R1.Pin_1

notes:
  Green button is the button that gets pressed by the vacuum
  +5V from USB

custom parts:
  Particle - Photon2: The Photon 2 is a microcontroller and Wi-Fi networking developed by particle. Features: 802.11a/b/g/n Wi-Fi, 2.4 GHz and 5 GHz Integrated PCB antenna Integrated U.FL connector for external antenna Integrated RF switch BLE 5 using same antenna as Wi-Fi Realtek RTL8721DM MCU ARM Cortex M33 CPU, 200 MHz 2048 KB (2 MB) user application maximum size 3072 KB (3 MB) of RAM available to user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
  Pushbutton: A generic pushbutton.
