# Fritzing sketch VacuumATM (saved by Fritzing 1.0.1rc)
circuit board: 8.46667cm x 5.64444cm
breadboards: 1

parts:
  A1 = Particle - Photon2
  M1 = Dagu DGServo 9g (Top view) [part_number=RS001B]
  S1 = Pushbutton [package="[THT]"]
  J2 = Power Jack [package=power_jack_slot]
  S3 = Momentary Switch [package=ksa_sealed_tac_switch]
  Part1 = 16 NeoPixel Ring [part_number=1463]
  NEOPIXEL1 = Neopixel Strip -- Black (30/m)

nets:
  N1: A1.Pin_1, A1.Pin_40, S3.4
  3.3V: A1.Pin_2, S1.Pin_3, S1.Pin_4
  GND: A1.Pin_4, M1.gnd, J2.GND, S3.2, Part1.GND, NEOPIXEL1.GND
  N2: A1.Pin_8, M1.pulse
  N3: A1.Pin_10, S1.Pin_1, S1.Pin_2
  N4: A1.Pin_19, Part1.IN
  0V/5V: A1.Pin_26, M1.vcc, J2.PWR, Part1.VDD, NEOPIXEL1.+5V
  N5: Part1.OUT, NEOPIXEL1.Din

notes:
  Blue button represents the microswitch that gets pressed by the cam.
  +5V from USB

custom parts:
  Particle - Photon2: The Photon 2 is a microcontroller and Wi-Fi networking developed by particle. Features: 802.11a/b/g/n Wi-Fi, 2.4 GHz and 5 GHz Integrated PCB antenna Integrated U.FL connector for external antenna Integrated RF switch BLE 5 using same antenna as Wi-Fi Realtek RTL8721DM MCU ARM Cortex M33 CPU, 200 MHz 2048 KB (2 MB) user application maximum size 3072 KB (3 MB) of RAM available to user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
  Pushbutton: A generic pushbutton.
  16 NeoPixel Ring: 16 ultra bright smart LED NeoPixels are arranged in a circle with 1.75" (44.5mm) outer diameter. The rings are 'chainable' - connect the output pin of one to the input pin of another. Use only one microcontroller pin to control as many as you can chain together! Each LED is addressable as the driver chip is inside the LED. Each one has ~18mA constant current drive so the color will be very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
  Neopixel Strip -- Black (30/m): These NeoPixel strips have 30 digitally-addressable pixel LEDs per meter and are very affordable and are only 12.5 mm wide, 10 mm if you remove the strip from the casing.
